# Fritzing sketch Microprocessor_Project_Circuit_Schematic (saved by Fritzing 1.0.2b)

parts:
  부품1 = Arduino Uno (Rev3) - ICSP
  MIC5 = Microphone
  MIC6 = Microphone
  MIC4 = Microphone
  MIC22 = Microphone
  MIC3 = Microphone
  MIC15 = Microphone
  MIC18 = Microphone
  MIC16 = Microphone
  MIC7 = Microphone
  MIC14 = Microphone
  MIC17 = Microphone
  MIC21 = Microphone
  MIC13 = Microphone
  MIC20 = Microphone
  MIC19 = Microphone
  MIC10 = Microphone
  Transducer = Microphone
  MIC8 = Microphone
  MIC9 = Microphone
  MIC23 = Microphone
  MIC24 = Microphone
  MIC25 = Microphone
  MIC26 = Microphone
  MIC27 = Microphone
  MIC28 = Microphone
  MIC29 = Microphone
  MIC30 = Microphone
  L298N1_Motor_Driver = L298N DC motor driver
  MIC31 = Microphone
  MIC32 = Microphone
  Arduino_Nano = Arduino Nano (Rev3.0)
  J1 = Basic Servo  # not connected
  MIC11 = Microphone
  Slide_Switch = SPDT Slide Switch [package=ayz0202]
  DC_connector = Power Jack [package=power_jack_combo]
  Lipo_Battery = LIPO-1000mAh [package=lipo-1000]
  S1 = Pushbutton [package=THT]
  S2 = Pushbutton [package=THT]
  push_button = Pushbutton [package=THT]

nets:
  N1: 부품1.D10_PWM/SS, 부품1.D11_PWM/MOSI
  N2: MIC5.pin1, MIC4.pin1, MIC3.pin1
  N3: MIC6.pin1, MIC31.pin1, MIC32.pin1
  N4: MIC22.pin1, MIC15.pin1, MIC16.pin1, MIC21.pin1, MIC20.pin1
  N5: MIC22.pin2, MIC15.pin2, MIC16.pin2, MIC21.pin2, MIC20.pin2, L298N1_Motor_Driver.OUT2
  N6: MIC18.pin1, MIC14.pin1, MIC13.pin1, MIC19.pin1, MIC8.pin1
  N7: MIC18.pin2, MIC14.pin2, MIC13.pin2, MIC19.pin2, MIC8.pin2, L298N1_Motor_Driver.OUT4
  N8: MIC7.pin1, MIC17.pin1, MIC23.pin1, MIC24.pin1, MIC25.pin1, MIC26.pin1, MIC27.pin1
  N9: MIC7.pin2, MIC17.pin2, MIC23.pin2, MIC24.pin2, MIC25.pin2, MIC26.pin2, MIC27.pin2, L298N1_Motor_Driver.OUT3
  N10: MIC10.pin1, Transducer.pin1, MIC9.pin1, MIC28.pin1, MIC29.pin1, MIC30.pin1, L298N1_Motor_Driver.GND, MIC11.pin1
  N11: MIC10.pin2, Transducer.pin2, MIC9.pin2, MIC28.pin2, MIC29.pin2, MIC30.pin2, L298N1_Motor_Driver.OUT1, MIC11.pin2
  N12: L298N1_Motor_Driver.IN1, Arduino_Nano.A3
  N13: L298N1_Motor_Driver.IN2, Arduino_Nano.A2
  N14: L298N1_Motor_Driver.IN3, Arduino_Nano.A1
  N15: L298N1_Motor_Driver.IN4, Arduino_Nano.A0
  N16: Arduino_Nano.GND, S1.leg1
  N17: Arduino_Nano.D2, S1.leg0
  N18: Arduino_Nano.D3, S2.leg0
  N19: Arduino_Nano.D4, push_button.leg0
  N20: Arduino_Nano.D10, Arduino_Nano.D11/MOSI
  N21: Slide_Switch.3, DC_connector.PWR
  N22: Slide_Switch.1, Lipo_Battery.+
  N23: Slide_Switch.6, Lipo_Battery.-
  N24: Slide_Switch.4, DC_connector.GND

notes:
  총 트랜스듀서 30(24)개
  (- 1st floor 없다는 가정)
  트랜스듀서 배치 시 GND 가 오목한 반구 중심점 방향 향하도록
  밑에 reference image 참조
  maybe.. 초록선 / 핑크선으로 결선할 수는 있을 듯?
  DC-DC Boost Converter
  배터리 오링 났을 때 사용하기 위한 추가 외부 전원 (Optional)
  Power Line

custom parts:
  L298N DC motor driver: 2x DC motor driver with 78M05 positive voltage regulator (7..35 V) L298N: max 46 V, 2 A Set 5 V Enable jumper to enable 5 V regultor (needed for the L298N) and +5 V output at screw terminal or supply external +5 V at screw terminal Set ENA and/or ENB to +5 V to enable motor permanently or supply ENA and/or ENB with PWM signal IN1 and IN2 set rotation directory for motor A (OUT1/OUT2) IN2 and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
